# Fritzing sketch RPi_RGB_Strip_Blueprint (saved by Fritzing 0.8.7b)
breadboards: 1

parts:
  Raspberry_Pi_1 = Raspberry Pi 3
  Q2 = Basic FET N-Channel [package="TO220 [THT]"]
  Q3 = Basic FET N-Channel [package="TO220 [THT]"]
  Q4 = Basic FET N-Channel [package="TO220 [THT]"]
  J1 = Power Jack [package=power_jack_combo]
  RGB_Strip_LED3 = RGB Strip LED

nets:
  N1: Raspberry_Pi_1.GIPO17, Q3.gate
  N2: Raspberry_Pi_1.GIPO22, Q2.gate
  N3: Raspberry_Pi_1.GIPO24, Q4.gate
  GND: Raspberry_Pi_1.GND, Q2.source, Q3.source, Q4.source, J1.GND
  N4: Q2.drain, RGB_Strip_LED3.Green_Connect
  N5: Q3.drain, RGB_Strip_LED3.Red_Connect
  N6: Q4.drain, RGB_Strip_LED3.Blue_Connect
  N7: J1.PWR, RGB_Strip_LED3.Common_Connect

custom parts:
  RGB Strip LED: A tri-color Strip LED with red, green and blue. Based on LED SMD 5050 RGB Pin order: common cathode - green - red - blue
