# Fritzing sketch RPi_RGB_Strip_With_LED_Breakout_View_Blueprint (saved by Fritzing 0.8.7b)
breadboards: 1

parts:
  Raspberry_Pi_1 = Raspberry Pi 3
  J1 = Power Jack [package=power_jack_combo]
  RGB_Strip_LED3 = RGB Strip LED
  R1 = Resistor [tolerance=±5% resistance=330 package=THT]
  R2 = Resistor [tolerance=±5% resistance=330 package=THT]
  R3 = Resistor [tolerance=±5% resistance=330 package=THT]
  LED2 = LED - 5mm [color="Red (633nm)" package="5 mm [THT]"]
  LED3 = LED - 5mm [color="Green (555nm)" package="5 mm [THT]"]
  LED4 = LED - 5mm [color="Blue (430nm)" package="5 mm [THT]"]
  LED5 = RGB LED (com. anode, rbg) [package="5 mm [THT]"]
  Q1 = Basic FET N-Channel [package="TO220 [THT]"]
  Q2 = Basic FET N-Channel [package="TO220 [THT]"]
  Q3 = Basic FET N-Channel [package="TO220 [THT]"]

nets:
  N1: Raspberry_Pi_1.GIPO17, R1.Pin_0, Q1.gate
  N2: Raspberry_Pi_1.GIPO22, R3.Pin_0, Q2.gate
  N3: Raspberry_Pi_1.GIPO24, R2.Pin_0, Q3.gate
  GND: Raspberry_Pi_1.GND, J1.GND, LED2.cathode, LED3.cathode, LED4.cathode, LED5.common_anode, Q1.source, Q2.source, Q3.source
  N4: J1.PWR, RGB_Strip_LED3.Common_Connect
  N5: RGB_Strip_LED3.Green_Connect, Q2.drain
  N6: RGB_Strip_LED3.Red_Connect, Q1.drain
  N7: RGB_Strip_LED3.Blue_Connect, Q3.drain
  N8: R1.Pin_1, LED2.anode, LED5.red_cathode
  N9: R2.Pin_1, LED4.anode, LED5.green_cathode
  N10: R3.Pin_1, LED3.anode, LED5.blue_cathode

custom parts:
  RGB Strip LED: A tri-color Strip LED with red, green and blue. Based on LED SMD 5050 RGB Pin order: common cathode - green - red - blue
